// Digital circuit eater_8bit_relay.dig as structural Verilog
module eater_8bit_relay (
  input  clk,
  input  HALT,
  input  in_3,
  input  clk_2,
  input  clk_3,
  input  in_6,
  input  clk_4,
  input  MANUAL,
  input  in_9,
  input  in_10,
  input  in_11,
  input  in_12,
  input  in_13,
  input  in_14,
  input  in_15,
  input  in_16,
  input  SELECT,
  input  in_18,
  input  in_19,
  input  in_20,
  input  in_21,
  input  in_22,
  input  in_23,
  input  in_24,
  input  in_25,
  input  in_26,
  input  [7:0] _1,
  input  in_28,
  input  in_29,
  input  in_30,
  input  [2:0] in_31,
  input  in_32,
  input  in_33,
  input  in_34,
  input  in_35,
  input  in_36,
  input  in_37,
  input  [3:0] _1_2,
  input  in_39,
  input  in_40,
  input  in_41,
  input  in_42
);

  wire and_1_out, and_2_out, B_SIGN, CARRY, CLOCK, nCLOCK, or_1_out, or_2_out, or_3_out, or_4_out, or_5_out,
       or_8_out, or_9_out, relay_1_p2, relay_2_p2, relay_3_p2, relay_4_p2, relay_5_p2, relay_6_p2,
       relay_7_p2, relay_8_p2, relay_9_p2, relay_10_p2, relay_11_p2, relay_12_p2, relay_13_p2, relay_14_p2,
       relay_15_p4, relay_16_p4, relay_17_p4, relay_18_p4, relay_19_p4, relay_20_p4, relay_21_p4,
       relay_22_p4, relay_23_p4, relay_24_p4, relay_25_p4, relay_26_p4, relay_27_p4, relay_28_p4,
       relay_29_p4, relay_30_p4, relay_31_p4, relay_32_p4, relay_33_p4, relay_35_p4, relay_36_p4,
       relay_37_p4, relay_38_p4, relay_40_p4, relay_41_p4, relay_42_p4, relay_43_p4, relay_47_p3,
       relay_47_p4, relay_49_p2, relay_50_p4, relay_51_p3, relay_52_p2, relay_53_p4, relay_54_p4,
       relay_55_p4, relay_57_p2, relay_59_p4, relay_64_p4, relay_65_p4, relaydt_1_p8, relaydt_2_p8,
       relaydt_3_p8, relaydt_4_p8, relaydt_6_p7, relaydt_6_p8, relaydt_7_p5, relaydt_7_p6, relaydt_9_p4,
       relaydt_9_p5, relaydt_11_p4, relaydt_11_p5, relaydt_13_p4, relaydt_13_p5, relaydt_15_p3,
       relaydt_15_p5, relaydt_15_p6, relaydt_16_p2, relaydt_55_p1, relaydt_55_p4, relaydt_55_p6,
       relaydt_57_p1, relaydt_57_p4, relaydt_57_p6, relaydt_58_p3, relaydt_58_p6, relaydt_58_p9,
       relaydt_58_p12, relaydt_58_p17, relaydt_60_p1, relaydt_60_p4, relaydt_60_p5, relaydt_60_p7,
       relaydt_60_p8, relaydt_60_p10, relaydt_61_p1, relaydt_61_p4, relaydt_61_p5, relaydt_61_p7,
       relaydt_61_p8, relaydt_61_p10, relaydt_62_p4, relaydt_62_p6, relaydt_62_p7, relaydt_67_p3,
       relaydt_67_p5, relaydt_68_p1, relaydt_68_p2, relaydt_69_p1, relaydt_69_p2, relaydt_70_p1,
       relaydt_70_p4, relaydt_70_p5, relaydt_70_p7, relaydt_70_p8, relaydt_70_p10, relaydt_71_p3,
       relaydt_71_p6, relaydt_71_p9, relaydt_71_p14, relaydt_74_p4, relaydt_74_p6, relaydt_76_p4,
       relaydt_76_p6, relaydt_79_p1, relaydt_79_p4, relaydt_79_p5, relaydt_79_p7, relaydt_79_p8,
       relaydt_79_p10, relaydt_80_p1, relaydt_80_p4, relaydt_80_p5, relaydt_80_p7, relaydt_80_p8,
       relaydt_80_p10, relaydt_82_p4, relaydt_82_p6, relaydt_83_p1, relaydt_83_p2, relaydt_84_p1,
       relaydt_84_p4, relaydt_84_p5, relaydt_84_p7, relaydt_84_p8, relaydt_84_p10, relaydt_85_p3,
       relaydt_85_p6, relaydt_85_p9, relaydt_85_p14, relaydt_88_p4, relaydt_88_p6, relaydt_89_p1,
       relaydt_89_p2, relaydt_91_p4, relaydt_91_p6, relaydt_92_p1, relaydt_92_p2, relaydt_94_p4,
       relaydt_94_p6, relaydt_94_p7, relaydt_95_p1, relaydt_95_p4, relaydt_95_p5, relaydt_95_p7,
       relaydt_95_p8, relaydt_95_p10, relaydt_96_p1, relaydt_96_p4, relaydt_96_p5, relaydt_96_p7,
       relaydt_96_p8, relaydt_96_p10, relaydt_99_p1, relaydt_99_p2, relaydt_102_p4, relaydt_102_p6,
       relaydt_103_p3, relaydt_103_p6, relaydt_103_p9, relaydt_103_p14, relaydt_105_p1, relaydt_105_p2,
       relaydt_106_p1, relaydt_106_p2, relaydt_107_p6, relaydt_108_p1, relaydt_108_p4, relaydt_108_p5,
       relaydt_108_p7, relaydt_108_p8, relaydt_108_p10, relaydt_110_p4, relaydt_110_p6, relaydt_112_p4,
       relaydt_112_p6, relaydt_113_p6, relaydt_116_p1, relaydt_116_p4, relaydt_116_p5, relaydt_116_p7,
       relaydt_116_p8, relaydt_116_p10, relaydt_117_p1, relaydt_117_p4, relaydt_117_p5, relaydt_117_p7,
       relaydt_117_p8, relaydt_117_p10, relaydt_118_p6, relaydt_120_p1, relaydt_120_p2, relaydt_121_p3,
       relaydt_121_p6, relaydt_121_p9, relaydt_121_p14, relaydt_126_p4, relaydt_126_p6, relaydt_127_p1,
       relaydt_127_p2, relaydt_128_p1, relaydt_128_p2, relaydt_129_p6, relaydt_131_p1, relaydt_131_p5,
       relaydt_131_p6, relaydt_131_p8, relaydt_133_p4, relaydt_133_p6, relaydt_135_p4, relaydt_135_p6,
       relaydt_136_p6, relaydt_137_p3, relaydt_137_p6, relaydt_137_p9, relaydt_137_p14, relaydt_139_p1,
       relaydt_139_p4, relaydt_139_p5, relaydt_139_p7, relaydt_139_p8, relaydt_139_p10, relaydt_140_p1,
       relaydt_140_p4, relaydt_140_p5, relaydt_140_p7, relaydt_140_p8, relaydt_140_p10, relaydt_141_p6,
       relaydt_144_p1, relaydt_144_p2, relaydt_144_p15, relaydt_145_p6, relaydt_147_p1, relaydt_147_p2,
       relaydt_148_p1, relaydt_148_p2, relaydt_150_p3, relaydt_150_p4, relaydt_151_p3, relaydt_151_p6,
       relaydt_151_p9, relaydt_151_p14, relaydt_154_p4, relaydt_154_p6, relaydt_156_p4, relaydt_156_p6,
       relaydt_160_p1, relaydt_160_p4, relaydt_160_p5, relaydt_160_p7, relaydt_160_p8, relaydt_160_p10,
       relaydt_161_p1, relaydt_161_p4, relaydt_161_p5, relaydt_161_p7, relaydt_161_p8, relaydt_161_p10,
       relaydt_163_p3, relaydt_163_p6, relaydt_163_p9, relaydt_166_p4, relaydt_166_p6, relaydt_167_p1,
       relaydt_167_p2, relaydt_169_p4, relaydt_169_p6, relaydt_170_p1, relaydt_170_p2, relaydt_171_p1,
       relaydt_171_p4, relaydt_171_p5, relaydt_171_p7, relaydt_171_p8, relaydt_171_p10, relaydt_172_p1,
       relaydt_172_p4, relaydt_172_p5, relaydt_172_p7, relaydt_172_p8, relaydt_172_p10, relaydt_173_p11,
       relaydt_173_p12, relaydt_173_p13, relaydt_173_p14, relaydt_176_p1, relaydt_176_p2, relaydt_177_p1,
       relaydt_177_p2, relaydt_178_p1, relaydt_178_p5, relaydt_178_p9, relaydt_178_p13, relaydt_178_p25,
       relaydt_180_p4, relaydt_180_p6, relaydt_182_p4, relaydt_182_p6, relaydt_184_p1, relaydt_184_p5,
       relaydt_184_p6, relaydt_184_p8, relaydt_185_p1, relaydt_185_p5, relaydt_185_p6, relaydt_185_p8,
       relaydt_186_p1, relaydt_186_p2, relaydt_187_p1, relaydt_187_p2, rs_ff_1_nq, rs_ff_1_q, STEP_out, ZERO;
  wire [0:0] relay_19_p5, relaydt_32_p3, relaydt_36_p3, relaydt_37_p3, relaydt_40_p3, relaydt_41_p3,
       relaydt_44_p3, relaydt_45_p3, relaydt_48_p3, relaydt_49_p3, relaydt_52_p3, relaydt_53_p3,
       relaydt_72_p14, relaydt_86_p3, relaydt_86_p6, relaydt_86_p9, relaydt_86_p14, relaydt_100_p1,
       relaydt_104_p3, relaydt_104_p6, relaydt_104_p9, relaydt_104_p14, relaydt_105_p11, relaydt_106_p11,
       relaydt_120_p11, relaydt_122_p3, relaydt_122_p6, relaydt_122_p9, relaydt_122_p14, relaydt_123_p1,
       relaydt_127_p11, relaydt_128_p11, relaydt_130_p1, relaydt_138_p3, relaydt_138_p6, relaydt_138_p9,
       relaydt_138_p14, relaydt_142_p1, relaydt_144_p11, relaydt_146_p1, relaydt_147_p11, relaydt_148_p11,
       relaydt_149_p1, relaydt_152_p3, relaydt_152_p6, relaydt_152_p9, relaydt_152_p14, relaydt_164_p3,
       relaydt_164_p6, relaydt_164_p10, relaydt_167_p11, relaydt_170_p11, relaydt_176_p11, relaydt_177_p11,
       relaydt_186_p11, relaydt_187_p11;
  wire [1:0] relaydt_14_p2, relaydt_22_p2, relaydt_59_p3, relaydt_59_p6, relaydt_59_p9, relaydt_59_p12,
       relaydt_68_p11, relaydt_69_p11, relaydt_83_p11, relaydt_114_p1;
  wire [2:0] SCZ;
  wire [3:0] binary_to_bcd_1__1s, binary_to_bcd_1__10s, binary_to_bcd_1__100s, CIncrement, INST, REG_COUNT,
       relaydt_78_p5;
  wire [6:0] REG_B;
  wire [7:0] BUS, REG_C, relaydt_1_p5, relaydt_2_p5, relaydt_3_p5, relaydt_4_p5, relaydt_5_p5, relaydt_63_p5;
  wire [15:0] R2_d;

  or or_1 (or_1_out, in_20, in_42);
  or or_2 (or_2_out, in_19, in_42);
  or or_3 (or_3_out, in_34, in_42);
  or or_4 (or_4_out, in_32, in_42);
  // Relay relay_1: pin names not known; wires that end beside it: or_1_out, relay_1_p2
  // RelayDT #(.Bits(8)) relaydt_1: pin names not known; wires that end beside it: in_42, {8{1'b0}}, BUS, 1'b0, relaydt_1_p5, CLOCK, 1'b0, relaydt_1_p8, 1'b0
  // Relay relay_2: pin names not known; wires that end beside it: or_2_out, relay_2_p2
  // RelayDT #(.Bits(8)) relaydt_2: pin names not known; wires that end beside it: in_42, {8{1'b0}}, BUS, 1'b0, relaydt_2_p5, CLOCK, 1'b0, relaydt_2_p8, 1'b0
  // Relay relay_3: pin names not known; wires that end beside it: or_3_out, relay_3_p2
  // RelayDT #(.Bits(8)) relaydt_3: pin names not known; wires that end beside it: in_42, {8{1'b0}}, BUS, 1'b0, relaydt_3_p5, CLOCK, 1'b0, relaydt_3_p8, 1'b0
  // Relay relay_4: pin names not known; wires that end beside it: or_4_out, relay_4_p2
  // RelayDT #(.Bits(8)) relaydt_4: pin names not known; wires that end beside it: in_42, {8{1'b0}}, BUS, 1'b0, relaydt_4_p5, CLOCK, 1'b0, relaydt_4_p8, 1'b0
  or or_5 (or_5_out, in_35, in_42);
  // RelayDT #(.Bits(8)) relaydt_5: pin names not known; wires that end beside it: in_42, {8{1'b0}}, BUS, 1'b0, relaydt_5_p5, CLOCK, 1'b0
  // Relay relay_5: pin names not known; wires that end beside it: relaydt_1_p5[7], relay_5_p2
  // Relay relay_6: pin names not known; wires that end beside it: relaydt_2_p5[7], relay_6_p2
  // Relay relay_7: pin names not known; wires that end beside it: relaydt_3_p5[7], relay_7_p2
  // Relay relay_8: pin names not known; wires that end beside it: relaydt_4_p5[7], relay_8_p2
  // Relay relay_9: pin names not known; wires that end beside it: or_5_out, relay_9_p2
  // RelayDT #(.poles(2)) relaydt_6: pin names not known; wires that end beside it: in_6, clk_3, clk_2, clk, clk_4, 1'b0, relaydt_6_p7, relaydt_6_p8, in_3, relaydt_6_p7, relaydt_6_p8
  // RelayDT #(.poles(2)) relaydt_7: pin names not known; wires that end beside it: relay_1_p2, 1'b1, relay_5_p2, 1'b0, relaydt_7_p5, relaydt_7_p6, 1'b0, relaydt_7_p5, 1'b0
  // RelayDT #(.poles(2)) relaydt_8: pin names not known; wires that end beside it: relay_5_p2, B_SIGN, 1'b0, relaydt_7_p6, 1'b1, 1'b0
  LED led_1 (.in(B_SIGN));
  // RelayDT #(.poles(2)) relaydt_9: pin names not known; wires that end beside it: relay_2_p2, 1'b1, relay_6_p2, relaydt_9_p4, relaydt_9_p5, 1'b0, relaydt_9_p4, 1'b0
  // RelayDT #(.poles(2)) relaydt_10: pin names not known; wires that end beside it: relay_6_p2, REG_C[7], 1'b0, relaydt_9_p5, 1'b1, 1'b0
  LED led_2 (.in(REG_C[7]));
  // RelayDT #(.poles(2)) relaydt_11: pin names not known; wires that end beside it: relay_3_p2, 1'b1, relay_7_p2, relaydt_11_p4, relaydt_11_p5, 1'b0, relaydt_11_p4, 1'b0
  // RelayDT #(.poles(2)) relaydt_12: pin names not known; wires that end beside it: relay_7_p2, INST[3], 1'b0, relaydt_11_p5, 1'b1, 1'b0
  LED led_3 (.in(INST[3]));
  // RelayDT #(.poles(2)) relaydt_13: pin names not known; wires that end beside it: relay_4_p2, 1'b1, relay_8_p2, relaydt_13_p4, relaydt_13_p5, 1'b0, relaydt_13_p4, 1'b0
  // RelayDT #(.poles(2)) relaydt_14: pin names not known; wires that end beside it: relay_8_p2, relaydt_14_p2[1], relaydt_13_p5, 1'b1, 1'b0
  // RelayDT #(.poles(2)) relaydt_15: pin names not known; wires that end beside it: relay_9_p2, 1'b1, relaydt_15_p3, 1'b0, relaydt_15_p5, relaydt_15_p6, 1'b0, relaydt_15_p5, 1'b0
  // Relay relay_10: pin names not known; wires that end beside it: relaydt_5_p5[3], relay_10_p2
  // RelayDT relaydt_16: pin names not known; wires that end beside it: 1'b0, relaydt_16_p2
  // RelayDT relaydt_17: pin names not known; wires that end beside it: 1'b1, relaydt_1_p8, relaydt_1_p8, 1'b0
  // Relay relay_11: pin names not known; wires that end beside it: relaydt_1_p5[6], relay_11_p2
  // RelayDT relaydt_18: pin names not known; wires that end beside it: 1'b1, relaydt_2_p8, relaydt_2_p8, 1'b0
  // Relay relay_12: pin names not known; wires that end beside it: relaydt_2_p5[6], relay_12_p2
  // RelayDT relaydt_19: pin names not known; wires that end beside it: 1'b1, relaydt_3_p8, relaydt_3_p8, 1'b0
  // Relay relay_13: pin names not known; wires that end beside it: relaydt_3_p5[6], relay_13_p2
  // RelayDT relaydt_20: pin names not known; wires that end beside it: 1'b1, relaydt_4_p8, relaydt_4_p8, 1'b0
  // Relay relay_14: pin names not known; wires that end beside it: relaydt_4_p5[6], relay_14_p2
  // RelayDT relaydt_21: pin names not known; wires that end beside it: 1'b1, relay_10_p2, relaydt_15_p3, 1'b0
  // RelayDT #(.poles(2)) relaydt_22: pin names not known; wires that end beside it: relay_10_p2, relaydt_22_p2[1], relaydt_15_p6, 1'b1, 1'b0
  LED led_4 (.in(relaydt_22_p2[1]));
  Button STEP (.out(STEP_out));
  and and_1 (and_1_out, STEP_out, MANUAL, ~HALT);  // And
  RS_FF rs_ff_1 (.S(and_2_out), .C(relaydt_16_p2), .R(~and_2_out), .Q(rs_ff_1_q), .nQ(rs_ff_1_nq));
  // RelayDT #(.poles(2)) relaydt_23: pin names not known; wires that end beside it: relay_11_p2, relay_11_p2, REG_B[6], 1'b0, relaydt_7_p6, 1'b1, 1'b0
  LED led_5 (.in(REG_B[6]));
  // RelayDT #(.poles(2)) relaydt_24: pin names not known; wires that end beside it: relay_12_p2, relay_12_p2, REG_C[6], 1'b0, relaydt_9_p5, 1'b1, 1'b0
  LED led_6 (.in(REG_C[6]));
  // RelayDT #(.poles(2)) relaydt_25: pin names not known; wires that end beside it: relay_13_p2, relay_13_p2, INST[2], 1'b0, relaydt_11_p5, 1'b1, 1'b0
  LED led_7 (.in(INST[2]));
  // RelayDT #(.poles(2)) relaydt_26: pin names not known; wires that end beside it: relay_14_p2, relay_14_p2, relaydt_14_p2[0], 1'b0, relaydt_13_p5, 1'b1, 1'b0
  and and_2 (and_2_out, ~MANUAL, ~HALT, rs_ff_1_nq);  // And
  // Relay relay_15: pin names not known; wires that end beside it: relaydt_15_p3, relaydt_5_p5[2], 1'b0, relay_15_p4
  LED led_8 (.in(relaydt_22_p2[0]));
  or or_6 (CLOCK, and_1_out, rs_ff_1_q);
  // Relay relay_16: pin names not known; wires that end beside it: relaydt_1_p8, relaydt_1_p5[5], 1'b0, relay_16_p4
  // Relay relay_17: pin names not known; wires that end beside it: relaydt_2_p8, relaydt_2_p5[5], 1'b0, relay_17_p4
  // Relay relay_18: pin names not known; wires that end beside it: relaydt_3_p8, relaydt_3_p5[5], 1'b0, relay_18_p4
  // Relay relay_19: pin names not known; wires that end beside it: relaydt_4_p8, relaydt_4_p5[5], 1'b0, relay_19_p4, relay_19_p5[0]
  // RelayDT #(.poles(2)) relaydt_27: pin names not known; wires that end beside it: relay_15_p4, relay_15_p4, relaydt_22_p2[0], 1'b0, relaydt_15_p6, 1'b1, 1'b0
  not not_1 (nCLOCK, CLOCK);
  // RelayDT #(.poles(2)) relaydt_28: pin names not known; wires that end beside it: relay_16_p4, relay_16_p4, REG_B[5], 1'b0, relaydt_7_p6, 1'b1, 1'b0
  LED led_9 (.in(REG_B[5]));
  // RelayDT #(.poles(2)) relaydt_29: pin names not known; wires that end beside it: relay_17_p4, relay_17_p4, REG_C[5], 1'b0, relaydt_9_p5, 1'b1, 1'b0
  LED led_10 (.in(REG_C[5]));
  // RelayDT #(.poles(2)) relaydt_30: pin names not known; wires that end beside it: relay_18_p4, relay_18_p4, INST[1], 1'b0, relaydt_11_p5, 1'b1, 1'b0
  LED led_11 (.in(INST[1]));
  // RelayDT #(.poles(2)) relaydt_31: pin names not known; wires that end beside it: relay_19_p4, relay_19_p4, relay_19_p5[0], 1'b0, relaydt_13_p5, 1'b1, 1'b0
  // Relay relay_20: pin names not known; wires that end beside it: relaydt_15_p3, relaydt_5_p5[1], 1'b0, relay_20_p4
  LED led_12 (.in(CLOCK));
  LED led_13 (.in(nCLOCK));
  // Relay relay_21: pin names not known; wires that end beside it: relaydt_1_p8, relaydt_1_p5[4], 1'b0, relay_21_p4
  // Relay relay_22: pin names not known; wires that end beside it: relaydt_2_p8, relaydt_2_p5[4], 1'b0, relay_22_p4
  // Relay relay_23: pin names not known; wires that end beside it: relaydt_3_p8, relaydt_3_p5[4], 1'b0, relay_23_p4
  // Relay relay_24: pin names not known; wires that end beside it: relaydt_4_p8, relaydt_4_p5[4], 1'b0, relay_24_p4
  // RelayDT #(.poles(2)) relaydt_32: pin names not known; wires that end beside it: relay_20_p4, relay_20_p4, relaydt_32_p3[0], 1'b0, relaydt_15_p6, 1'b1, 1'b0
  LED led_14 (.in(relaydt_32_p3[0]));
  // RelayDT #(.poles(2)) relaydt_33: pin names not known; wires that end beside it: relay_21_p4, relay_21_p4, REG_B[4], 1'b0, relaydt_7_p6, 1'b1, 1'b0
  LED led_15 (.in(REG_B[4]));
  // RelayDT #(.poles(2)) relaydt_34: pin names not known; wires that end beside it: relay_22_p4, relay_22_p4, REG_C[4], 1'b0, relaydt_9_p5, 1'b1, 1'b0
  LED led_16 (.in(REG_C[4]));
  // RelayDT #(.poles(2)) relaydt_35: pin names not known; wires that end beside it: relay_23_p4, relay_23_p4, INST[0], 1'b0, relaydt_11_p5, 1'b1, 1'b0
  LED led_17 (.in(INST[0]));
  // RelayDT #(.poles(2)) relaydt_36: pin names not known; wires that end beside it: relay_24_p4, relay_24_p4, relaydt_36_p3[0], 1'b0, relaydt_13_p5, 1'b1, 1'b0
  // Relay relay_25: pin names not known; wires that end beside it: relaydt_15_p3, relaydt_5_p5[0], 1'b0, relay_25_p4
  LED led_18 (.in(relaydt_37_p3[0]));
  // Relay relay_26: pin names not known; wires that end beside it: relaydt_1_p8, relaydt_1_p5[3], 1'b0, relay_26_p4
  // Relay relay_27: pin names not known; wires that end beside it: relaydt_2_p8, relaydt_2_p5[3], 1'b0, relay_27_p4
  // Relay relay_28: pin names not known; wires that end beside it: relaydt_3_p8, relaydt_3_p5[3], 1'b0, relay_28_p4
  // Relay relay_29: pin names not known; wires that end beside it: relaydt_4_p8, relaydt_4_p5[3], 1'b0, relay_29_p4
  // RelayDT #(.poles(2)) relaydt_37: pin names not known; wires that end beside it: relay_25_p4, relay_25_p4, relaydt_37_p3[0], 1'b0, relaydt_15_p6, 1'b1, 1'b0
  LED led_19 (.in(BUS[7]));
  // RelayDT #(.poles(2)) relaydt_38: pin names not known; wires that end beside it: relay_26_p4, relay_26_p4, REG_B[3], 1'b0, relaydt_7_p6, 1'b1, 1'b0
  LED led_20 (.in(REG_B[3]));
  // RelayDT #(.poles(2)) relaydt_39: pin names not known; wires that end beside it: relay_27_p4, relay_27_p4, REG_C[3], 1'b0, relaydt_9_p5, 1'b1, 1'b0
  LED led_21 (.in(REG_C[3]));
  // RelayDT #(.poles(2)) relaydt_40: pin names not known; wires that end beside it: relay_28_p4, relay_28_p4, relaydt_40_p3[0], 1'b0, relaydt_11_p5, 1'b1, 1'b0
  LED led_22 (.in(relaydt_40_p3[0]));
  // RelayDT #(.poles(2)) relaydt_41: pin names not known; wires that end beside it: relay_29_p4, relay_29_p4, relaydt_41_p3[0], 1'b0, relaydt_13_p5, 1'b1, 1'b0
  LED led_23 (.in(BUS[6]));
  LED led_24 (.in(BUS[5]));
  LED led_25 (.in(BUS[4]));
  LED led_26 (.in(BUS[3]));
  // Relay relay_30: pin names not known; wires that end beside it: relaydt_1_p8, relaydt_1_p5[2], 1'b0, relay_30_p4
  // Relay relay_31: pin names not known; wires that end beside it: relaydt_2_p8, relaydt_2_p5[2], 1'b0, relay_31_p4
  // Relay relay_32: pin names not known; wires that end beside it: relaydt_3_p8, relaydt_3_p5[2], 1'b0, relay_32_p4
  // Relay relay_33: pin names not known; wires that end beside it: relaydt_4_p8, relaydt_4_p5[2], 1'b0, relay_33_p4
  // Relay #(.Bits(8)) relay_34: pin names not known; wires that end beside it: SELECT, {in_16, in_15, in_14, in_13, in_12, in_11, in_10, in_9}, 1'b0
  LED led_27 (.in(BUS[2]));
  LED led_28 (.in(BUS[1]));
  LED led_29 (.in(BUS[0]));
  // RelayDT #(.poles(2)) relaydt_42: pin names not known; wires that end beside it: relay_30_p4, relay_30_p4, REG_B[2], 1'b0, relaydt_7_p6, 1'b1, 1'b0
  LED led_30 (.in(REG_B[2]));
  // RelayDT #(.poles(2)) relaydt_43: pin names not known; wires that end beside it: relay_31_p4, relay_31_p4, REG_C[2], 1'b0, relaydt_9_p5, 1'b1, 1'b0
  LED led_31 (.in(REG_C[2]));
  // RelayDT #(.poles(2)) relaydt_44: pin names not known; wires that end beside it: relay_32_p4, relay_32_p4, relaydt_44_p3[0], 1'b0, relaydt_11_p5, 1'b1, 1'b0
  LED led_32 (.in(relaydt_44_p3[0]));
  // RelayDT #(.poles(2)) relaydt_45: pin names not known; wires that end beside it: relay_33_p4, relay_33_p4, relaydt_45_p3[0], 1'b0, relaydt_13_p5, 1'b1, 1'b0
  RAMDualPort #(.AddrBits(4), .isProgramMemory("true"), .Bits(16)) R2 (
    .A({relaydt_22_p2, relaydt_32_p3[0], relaydt_37_p3[0]}), .Din({{8{1'b0}}, BUS}), .str(in_37), .C(CLOCK),
    .ld(1'b1), .D(R2_d));
  LED led_33 (.in(R2_d[6]));
  LED led_34 (.in(R2_d[7]));
  Binary_to_BCD binary_to_bcd_1 (
    .In({relaydt_14_p2, relay_19_p5[0], relaydt_36_p3[0], relaydt_41_p3[0], relaydt_45_p3[0], relaydt_49_p3[0], relaydt_53_p3[0]}),
    ._100s(binary_to_bcd_1__100s), ._10s(binary_to_bcd_1__10s), ._1s(binary_to_bcd_1__1s));
  LED led_35 (.in(R2_d[2]));
  LED led_36 (.in(R2_d[3]));
  LED led_37 (.in(R2_d[4]));
  LED led_38 (.in(R2_d[5]));
  // Relay relay_35: pin names not known; wires that end beside it: relaydt_1_p8, relaydt_1_p5[1], 1'b0, relay_35_p4
  // Relay relay_36: pin names not known; wires that end beside it: relaydt_2_p8, relaydt_2_p5[1], 1'b0, relay_36_p4
  // Relay relay_37: pin names not known; wires that end beside it: relaydt_3_p8, relaydt_3_p5[1], 1'b0, relay_37_p4
  // Relay relay_38: pin names not known; wires that end beside it: relaydt_4_p8, relaydt_4_p5[1], 1'b0, relay_38_p4
  Seven_Seg_Hex seven_seg_hex_1 (.d(binary_to_bcd_1__100s), .dp(1'b0));
  LED led_39 (.in(R2_d[0]));
  LED led_40 (.in(R2_d[1]));
  // RelayDT #(.poles(2)) relaydt_46: pin names not known; wires that end beside it: relay_35_p4, relay_35_p4, REG_B[1], 1'b0, relaydt_7_p6, 1'b1, 1'b0
  LED led_41 (.in(REG_B[1]));
  // RelayDT #(.poles(2)) relaydt_47: pin names not known; wires that end beside it: relay_36_p4, relay_36_p4, REG_C[1], 1'b0, relaydt_9_p5, 1'b1, 1'b0
  LED led_42 (.in(REG_C[1]));
  // RelayDT #(.poles(2)) relaydt_48: pin names not known; wires that end beside it: relay_37_p4, relay_37_p4, relaydt_48_p3[0], 1'b0, relaydt_11_p5, 1'b1, 1'b0
  LED led_43 (.in(relaydt_48_p3[0]));
  // RelayDT #(.poles(2)) relaydt_49: pin names not known; wires that end beside it: relay_38_p4, relay_38_p4, relaydt_49_p3[0], 1'b0, relaydt_13_p5, 1'b1, 1'b0
  Seven_Seg_Hex seven_seg_hex_2 (.d(binary_to_bcd_1__10s), .dp(1'b0));
  // Relay #(.Bits(8)) relay_39: pin names not known; wires that end beside it: in_36, R2_d[7:0], 1'b0, BUS
  // Relay relay_40: pin names not known; wires that end beside it: relaydt_1_p8, relaydt_1_p5[0], 1'b0, relay_40_p4
  // Relay relay_41: pin names not known; wires that end beside it: relaydt_2_p8, relaydt_2_p5[0], 1'b0, relay_41_p4
  // Relay relay_42: pin names not known; wires that end beside it: relaydt_3_p8, relaydt_3_p5[0], 1'b0, relay_42_p4
  // Relay relay_43: pin names not known; wires that end beside it: relaydt_4_p8, relaydt_4_p5[0], 1'b0, relay_43_p4
  Seven_Seg_Hex seven_seg_hex_3 (.d(binary_to_bcd_1__1s), .dp(1'b0));
  // RelayDT #(.poles(2)) relaydt_50: pin names not known; wires that end beside it: relay_40_p4, relay_40_p4, REG_B[0], 1'b0, relaydt_7_p6, 1'b1, 1'b0
  LED led_44 (.in(REG_B[0]));
  // RelayDT #(.poles(2)) relaydt_51: pin names not known; wires that end beside it: relay_41_p4, relay_41_p4, REG_C[0], 1'b0, relaydt_9_p5, 1'b1, 1'b0
  LED led_45 (.in(REG_C[0]));
  // RelayDT #(.poles(2)) relaydt_52: pin names not known; wires that end beside it: relay_42_p4, relay_42_p4, relaydt_52_p3[0], 1'b0, relaydt_11_p5, 1'b1, 1'b0
  LED led_46 (.in(relaydt_52_p3[0]));
  // RelayDT #(.poles(2)) relaydt_53: pin names not known; wires that end beside it: relay_43_p4, relay_43_p4, relaydt_53_p3[0], 1'b0, relaydt_13_p5, 1'b1, 1'b0
  // Relay #(.Bits(8)) relay_44: pin names not known; wires that end beside it: in_21, {B_SIGN, REG_B}, 1'b0, BUS
  // Relay #(.Bits(8)) relay_45: pin names not known; wires that end beside it: in_18, REG_C, 1'b0, BUS
  // Relay #(.Bits(8)) relay_46: pin names not known; wires that end beside it: in_33, {INST, relaydt_40_p3[0], relaydt_44_p3[0], relaydt_48_p3[0], relaydt_52_p3[0]}, 1'b0, BUS
  LED led_47 (.in(relaydt_59_p3[1]));
  or or_7 (CARRY, relaydt_57_p1, relaydt_55_p1);
  LED led_48 (.in(relaydt_59_p9[1]));
  LED led_49 (.in(relaydt_59_p6[1]));
  // RelayDT relaydt_54: pin names not known; wires that end beside it: 1'b0, 1'b1, 1'b0
  // RelayDT relaydt_55: pin names not known; wires that end beside it: relaydt_55_p1, 1'b0, 1'b1, relaydt_55_p4, relaydt_55_p4, relaydt_55_p6
  // RelayDT relaydt_56: pin names not known; wires that end beside it: 1'b0, 1'b1, 1'b0
  // RelayDT relaydt_57: pin names not known; wires that end beside it: relaydt_57_p1, 1'b0, 1'b1, relaydt_57_p4, relaydt_57_p4, relaydt_57_p6
  // Relay relay_47: pin names not known; wires that end beside it: CLOCK, in_28, relay_47_p3, relay_47_p4, 1'b0
  // RelayDT #(.poles(4)) relaydt_58: pin names not known; wires that end beside it: 1'b0, 1'b1, relaydt_58_p3, 1'b1, 1'b0, relaydt_58_p6, 1'b0, 1'b1, relaydt_58_p9, 1'b0, 1'b1, relaydt_58_p12, REG_C[7], 1'b0, 1'b0, 1'b1, relaydt_58_p17
  // RelayDT #(.poles(4)) relaydt_59: pin names not known; wires that end beside it: 1'b0, relaydt_58_p3, relaydt_59_p3[1], 1'b1, 1'b0, relaydt_59_p6[1], relaydt_58_p9, relaydt_58_p6, relaydt_59_p9[1], relaydt_58_p12, 1'b1, relaydt_59_p12[1], B_SIGN, 1'b0, 1'b0, relaydt_58_p17, relaydt_59_p3[0]
  LED led_50 (.in(relaydt_59_p12[1]));
  // RelayDT #(.poles(4)) relaydt_60: pin names not known; wires that end beside it: relaydt_60_p1, REG_C[7], relaydt_60_p1, relaydt_60_p4, relaydt_60_p5, 1'b0, relaydt_60_p7, relaydt_60_p8, relaydt_55_p6, relaydt_60_p10, relaydt_60_p10, relaydt_60_p7, relaydt_60_p8
  // RelayDT #(.poles(4)) relaydt_61: pin names not known; wires that end beside it: relaydt_61_p1, _1[7], relaydt_61_p1, relaydt_61_p4, relaydt_61_p5, 1'b0, relaydt_61_p7, relaydt_61_p8, relaydt_57_p6, relaydt_61_p10, relaydt_61_p10, relaydt_61_p7, relaydt_61_p8
  // RelayDT #(.poles(2)) relaydt_62: pin names not known; wires that end beside it: 1'b0, relay_47_p3, 1'b1, relaydt_62_p4, 1'b0, relaydt_62_p6, relaydt_62_p7, 1'b0, relaydt_62_p6, 1'b0
  // Relay relay_48: pin names not known; wires that end beside it: B_SIGN, relaydt_62_p4
  LED Sign (.in(SCZ[2]));
  // RelayDT #(.Bits(8)) relaydt_63: pin names not known; wires that end beside it: in_42, {8{1'b0}}, BUS, 1'b0, relaydt_63_p5
  LED led_51 (.in(relaydt_59_p3[0]));
  // RelayDT relaydt_64: pin names not known; wires that end beside it: 1'b1, relay_47_p4, relay_47_p4, 1'b0
  // RelayDT #(.poles(2)) relaydt_65: pin names not known; wires that end beside it: relaydt_62_p4, SCZ[2], relaydt_62_p7, 1'b1, 1'b0
  or or_8 (or_8_out, in_40, in_42);
  // RelayDT relaydt_66: pin names not known; wires that end beside it: 1'b0, 1'b1, 1'b0
  // RelayDT relaydt_67: pin names not known; wires that end beside it: 1'b0, 1'b1, relaydt_67_p3, relaydt_67_p3, relaydt_67_p5
  LED led_52 (.in(relaydt_59_p9[0]));
  LED led_53 (.in(relaydt_59_p6[0]));
  // RelayDT #(.poles(4)) relaydt_68: pin names not known; wires that end beside it: relaydt_68_p1, relaydt_68_p2, relaydt_55_p6, relaydt_60_p10, relaydt_60_p8, relaydt_68_p1, relaydt_68_p1, relaydt_68_p2, 1'b0, relaydt_60_p4, relaydt_68_p11[1], 1'b1, relaydt_60_p5, B_SIGN, 1'b0
  LED led_54 (.in(relaydt_68_p11[1]));
  // RelayDT #(.poles(4)) relaydt_69: pin names not known; wires that end beside it: relaydt_69_p1, relaydt_69_p2, relaydt_57_p6, relaydt_61_p10, relaydt_61_p8, relaydt_69_p1, relaydt_69_p1, relaydt_69_p2, 1'b0, relaydt_61_p4, relaydt_69_p11[1], 1'b1, relaydt_61_p5, B_SIGN, 1'b0
  LED led_55 (.in(relaydt_69_p11[1]));
  // Relay relay_49: pin names not known; wires that end beside it: CARRY, relay_49_p2
  or or_9 (or_9_out, in_39, in_42, or_8_out);
  // RelayDT #(.poles(4)) relaydt_70: pin names not known; wires that end beside it: relaydt_70_p1, _1_2[3], relaydt_70_p1, relaydt_70_p4, relaydt_70_p5, 1'b0, relaydt_70_p7, relaydt_70_p8, relaydt_67_p5, relaydt_70_p10, relaydt_70_p10, relaydt_70_p7, relaydt_70_p8
  // RelayDT #(.poles(4)) relaydt_71: pin names not known; wires that end beside it: 1'b1, 1'b0, relaydt_71_p3, 1'b0, 1'b1, relaydt_71_p6, 1'b0, 1'b1, relaydt_71_p9, REG_C[6], 1'b0, 1'b0, 1'b1, relaydt_71_p14
  // RelayDT #(.poles(4)) relaydt_72: pin names not known; wires that end beside it: 1'b1, 1'b0, relaydt_59_p6[0], relaydt_71_p6, relaydt_71_p3, relaydt_59_p9[0], relaydt_71_p9, 1'b1, relaydt_59_p12[0], REG_B[6], 1'b0, 1'b0, relaydt_71_p14, relaydt_72_p14[0]
  LED led_56 (.in(relaydt_59_p12[0]));
  // RelayDT relaydt_73: pin names not known; wires that end beside it: relaydt_60_p4, 1'b1, 1'b0
  // RelayDT relaydt_74: pin names not known; wires that end beside it: relaydt_60_p5, 1'b0, 1'b1, relaydt_74_p4, relaydt_74_p4, relaydt_74_p6
  // RelayDT relaydt_75: pin names not known; wires that end beside it: relaydt_61_p4, 1'b1, 1'b0
  // RelayDT relaydt_76: pin names not known; wires that end beside it: relaydt_61_p5, 1'b0, 1'b1, relaydt_76_p4, relaydt_76_p4, relaydt_76_p6
  // RelayDT #(.poles(2)) relaydt_77: pin names not known; wires that end beside it: relay_49_p2, relay_49_p2, SCZ[1], 1'b0, relaydt_62_p7, 1'b1, 1'b0
  LED u_Carry (.in(SCZ[1]));
  // RelayDT #(.Bits(4)) relaydt_78: pin names not known; wires that end beside it: or_8_out, relaydt_63_p5[3:0], CIncrement, 1'b0, relaydt_78_p5
  LED led_57 (.in(relaydt_72_p14[0]));
  // RelayDT #(.poles(4)) relaydt_79: pin names not known; wires that end beside it: relaydt_79_p1, REG_C[6], relaydt_79_p1, relaydt_79_p4, relaydt_79_p5, 1'b0, relaydt_79_p7, relaydt_79_p8, relaydt_74_p6, relaydt_79_p10, relaydt_79_p10, relaydt_79_p7, relaydt_79_p8
  // RelayDT #(.poles(4)) relaydt_80: pin names not known; wires that end beside it: relaydt_80_p1, _1[6], relaydt_80_p1, relaydt_80_p4, relaydt_80_p5, 1'b0, relaydt_80_p7, relaydt_80_p8, relaydt_76_p6, relaydt_80_p10, relaydt_80_p10, relaydt_80_p7, relaydt_80_p8
  // RelayDT relaydt_81: pin names not known; wires that end beside it: relaydt_70_p4, 1'b1, 1'b0
  // RelayDT relaydt_82: pin names not known; wires that end beside it: relaydt_70_p5, 1'b0, 1'b1, relaydt_82_p4, relaydt_82_p4, relaydt_82_p6
  // RelayDT #(.poles(4)) relaydt_83: pin names not known; wires that end beside it: relaydt_83_p1, relaydt_83_p2, relaydt_67_p5, relaydt_70_p10, relaydt_70_p8, relaydt_83_p1, relaydt_83_p1, relaydt_83_p2, 1'b0, relaydt_70_p4, relaydt_83_p11[1], 1'b1, relaydt_70_p5, REG_COUNT[3], 1'b0
  LED led_58 (.in(relaydt_83_p11[1]));
  LED led_59 (.in(relaydt_86_p6[0]));
  LED led_60 (.in(relaydt_86_p3[0]));
  // Relay relay_50: pin names not known; wires that end beside it: relay_47_p4, ZERO, 1'b0, relay_50_p4
  LED u_Zero (.in(SCZ[0]));
  // Relay relay_51: pin names not known; wires that end beside it: CLOCK, or_9_out, relay_51_p3
  // RelayDT #(.poles(4)) relaydt_84: pin names not known; wires that end beside it: relaydt_84_p1, _1_2[2], relaydt_84_p1, relaydt_84_p4, relaydt_84_p5, 1'b0, relaydt_84_p7, relaydt_84_p8, relaydt_82_p6, relaydt_84_p10, relaydt_84_p10, relaydt_84_p7, relaydt_84_p8
  // RelayDT #(.poles(4)) relaydt_85: pin names not known; wires that end beside it: 1'b1, 1'b0, relaydt_85_p3, 1'b0, 1'b1, relaydt_85_p6, 1'b0, 1'b1, relaydt_85_p9, REG_C[5], 1'b0, 1'b0, 1'b1, relaydt_85_p14
  // RelayDT #(.poles(4)) relaydt_86: pin names not known; wires that end beside it: 1'b1, 1'b0, relaydt_86_p3[0], relaydt_85_p6, relaydt_85_p3, relaydt_86_p6[0], relaydt_85_p9, 1'b1, relaydt_86_p9[0], REG_B[5], 1'b0, 1'b0, relaydt_85_p14, relaydt_86_p14[0]
  LED led_61 (.in(relaydt_86_p9[0]));
  // RelayDT relaydt_87: pin names not known; wires that end beside it: relaydt_79_p4, 1'b1, 1'b0
  // RelayDT relaydt_88: pin names not known; wires that end beside it: relaydt_79_p5, 1'b0, 1'b1, relaydt_88_p4, relaydt_88_p4, relaydt_88_p6
  // RelayDT #(.poles(4)) relaydt_89: pin names not known; wires that end beside it: relaydt_89_p1, relaydt_89_p2, relaydt_74_p6, relaydt_79_p10, relaydt_79_p8, relaydt_89_p1, relaydt_89_p1, relaydt_89_p2, 1'b0, relaydt_79_p4, relaydt_68_p11[0], 1'b1, relaydt_79_p5, REG_B[6], 1'b0
  LED led_62 (.in(relaydt_68_p11[0]));
  // RelayDT relaydt_90: pin names not known; wires that end beside it: relaydt_80_p4, 1'b1, 1'b0
  // RelayDT relaydt_91: pin names not known; wires that end beside it: relaydt_80_p5, 1'b0, 1'b1, relaydt_91_p4, relaydt_91_p4, relaydt_91_p6
  // RelayDT #(.poles(4)) relaydt_92: pin names not known; wires that end beside it: relaydt_92_p1, relaydt_92_p2, relaydt_76_p6, relaydt_80_p10, relaydt_80_p8, relaydt_92_p1, relaydt_92_p1, relaydt_92_p2, 1'b0, relaydt_80_p4, relaydt_69_p11[0], 1'b1, relaydt_80_p5, REG_B[6], 1'b0
  LED led_63 (.in(relaydt_69_p11[0]));
  // RelayDT #(.poles(2)) relaydt_93: pin names not known; wires that end beside it: relay_50_p4, relay_50_p4, SCZ[0], 1'b0, relaydt_62_p7, 1'b1, 1'b0
  // RelayDT #(.poles(2)) relaydt_94: pin names not known; wires that end beside it: 1'b0, relay_51_p3, 1'b1, relaydt_94_p4, 1'b0, relaydt_94_p6, relaydt_94_p7, 1'b0, relaydt_94_p6, 1'b0
  // Relay relay_52: pin names not known; wires that end beside it: relaydt_78_p5[3], relay_52_p2
  LED led_64 (.in(relaydt_86_p14[0]));
  // RelayDT #(.poles(4)) relaydt_95: pin names not known; wires that end beside it: relaydt_95_p1, REG_C[5], relaydt_95_p1, relaydt_95_p4, relaydt_95_p5, 1'b0, relaydt_95_p7, relaydt_95_p8, relaydt_88_p6, relaydt_95_p10, relaydt_95_p10, relaydt_95_p7, relaydt_95_p8
  // RelayDT #(.poles(4)) relaydt_96: pin names not known; wires that end beside it: relaydt_96_p1, _1[5], relaydt_96_p1, relaydt_96_p4, relaydt_96_p5, 1'b0, relaydt_96_p7, relaydt_96_p8, relaydt_91_p6, relaydt_96_p10, relaydt_96_p10, relaydt_96_p7, relaydt_96_p8
  // RelayDT relaydt_97: pin names not known; wires that end beside it: 1'b1, relay_52_p2, relaydt_94_p4, 1'b0
  // RelayDT #(.poles(2)) relaydt_98: pin names not known; wires that end beside it: relay_52_p2, REG_COUNT[3], relaydt_94_p7, 1'b1, 1'b0
  LED led_65 (.in(REG_COUNT[3]));
  // RelayDT #(.poles(4)) relaydt_99: pin names not known; wires that end beside it: relaydt_99_p1, relaydt_99_p2, relaydt_82_p6, relaydt_84_p10, relaydt_84_p8, relaydt_99_p1, relaydt_99_p1, relaydt_99_p2, 1'b0, relaydt_84_p4, relaydt_83_p11[0], 1'b1, relaydt_84_p5, REG_COUNT[2], 1'b0
  LED led_66 (.in(relaydt_104_p6[0]));
  LED led_67 (.in(relaydt_104_p3[0]));
  // RelayDT relaydt_100: pin names not known; wires that end beside it: relaydt_100_p1[0], 1'b1, 1'b0
  // RelayDT relaydt_101: pin names not known; wires that end beside it: relaydt_84_p4, 1'b1, 1'b0
  // RelayDT relaydt_102: pin names not known; wires that end beside it: relaydt_84_p5, 1'b0, 1'b1, relaydt_102_p4, relaydt_102_p4, relaydt_102_p6
  LED led_68 (.in(relaydt_83_p11[0]));
  // RelayDT #(.poles(4)) relaydt_103: pin names not known; wires that end beside it: 1'b1, 1'b0, relaydt_103_p3, 1'b0, 1'b1, relaydt_103_p6, 1'b0, 1'b1, relaydt_103_p9, REG_C[4], 1'b0, 1'b0, 1'b1, relaydt_103_p14
  // RelayDT #(.poles(4)) relaydt_104: pin names not known; wires that end beside it: 1'b1, 1'b0, relaydt_104_p3[0], relaydt_103_p6, relaydt_103_p3, relaydt_104_p6[0], relaydt_103_p9, 1'b1, relaydt_104_p9[0], REG_B[4], 1'b0, 1'b0, relaydt_103_p14, relaydt_104_p14[0]
  LED led_69 (.in(relaydt_104_p9[0]));
  // RelayDT #(.poles(4)) relaydt_105: pin names not known; wires that end beside it: relaydt_105_p1, relaydt_105_p2, relaydt_88_p6, relaydt_95_p10, relaydt_95_p8, relaydt_105_p1, relaydt_105_p1, relaydt_105_p2, 1'b0, relaydt_95_p4, relaydt_105_p11[0], 1'b1, relaydt_95_p5, REG_B[5], 1'b0
  // RelayDT #(.poles(4)) relaydt_106: pin names not known; wires that end beside it: relaydt_106_p1, relaydt_106_p2, relaydt_91_p6, relaydt_96_p10, relaydt_96_p8, relaydt_106_p1, relaydt_106_p1, relaydt_106_p2, 1'b0, relaydt_96_p4, relaydt_106_p11[0], 1'b1, relaydt_96_p5, REG_B[5], 1'b0
  // RelayDT relaydt_107: pin names not known; wires that end beside it: B_SIGN, 1'b0, 1'b1, B_SIGN, 1'b0, relaydt_107_p6, 1'b0
  LED led_70 (.in(relaydt_114_p1[1]));
  // Relay relay_53: pin names not known; wires that end beside it: relaydt_94_p4, relaydt_78_p5[2], 1'b0, relay_53_p4
  // RelayDT #(.poles(4)) relaydt_108: pin names not known; wires that end beside it: relaydt_108_p1, _1_2[1], relaydt_108_p1, relaydt_108_p4, relaydt_108_p5, 1'b0, relaydt_108_p7, relaydt_108_p8, relaydt_102_p6, relaydt_108_p10, relaydt_108_p10, relaydt_108_p7, relaydt_108_p8
  LED led_71 (.in(relaydt_104_p14[0]));
  // RelayDT relaydt_109: pin names not known; wires that end beside it: relaydt_95_p4, 1'b1, 1'b0
  // RelayDT relaydt_110: pin names not known; wires that end beside it: relaydt_95_p5, 1'b0, 1'b1, relaydt_110_p4, relaydt_110_p4, relaydt_110_p6
  LED led_72 (.in(relaydt_105_p11[0]));
  // RelayDT relaydt_111: pin names not known; wires that end beside it: relaydt_96_p4, 1'b1, 1'b0
  // RelayDT relaydt_112: pin names not known; wires that end beside it: relaydt_96_p5, 1'b0, 1'b1, relaydt_112_p4, relaydt_112_p4, relaydt_112_p6
  LED led_73 (.in(relaydt_106_p11[0]));
  // RelayDT relaydt_113: pin names not known; wires that end beside it: REG_B[6], 1'b0, relaydt_107_p6, REG_B[6], 1'b0, relaydt_113_p6, 1'b0
  // RelayDT relaydt_114: pin names not known; wires that end beside it: relaydt_114_p1[1], 1'b1, 1'b0
  LED led_74 (.in(relaydt_114_p1[0]));
  // RelayDT #(.poles(2)) relaydt_115: pin names not known; wires that end beside it: relay_53_p4, relay_53_p4, REG_COUNT[2], 1'b0, relaydt_94_p7, 1'b1, 1'b0
  LED led_75 (.in(REG_COUNT[2]));
  LED led_76 (.in(relaydt_122_p6[0]));
  LED led_77 (.in(relaydt_122_p3[0]));
  // RelayDT #(.poles(4)) relaydt_116: pin names not known; wires that end beside it: relaydt_116_p1, REG_C[4], relaydt_116_p1, relaydt_116_p4, relaydt_116_p5, 1'b0, relaydt_116_p7, relaydt_116_p8, relaydt_110_p6, relaydt_116_p10, relaydt_116_p10, relaydt_116_p7, relaydt_116_p8
  // RelayDT #(.poles(4)) relaydt_117: pin names not known; wires that end beside it: relaydt_117_p1, _1[4], relaydt_117_p1, relaydt_117_p4, relaydt_117_p5, 1'b0, relaydt_117_p7, relaydt_117_p8, relaydt_112_p6, relaydt_117_p10, relaydt_117_p10, relaydt_117_p7, relaydt_117_p8
  // RelayDT relaydt_118: pin names not known; wires that end beside it: REG_B[5], 1'b0, relaydt_113_p6, REG_B[5], 1'b0, relaydt_118_p6, 1'b0
  // RelayDT relaydt_119: pin names not known; wires that end beside it: relaydt_114_p1[0], 1'b1, 1'b0
  LED led_78 (.in(relaydt_123_p1[0]));
  // Relay relay_54: pin names not known; wires that end beside it: relaydt_94_p4, relaydt_78_p5[1], 1'b0, relay_54_p4
  // RelayDT #(.poles(4)) relaydt_120: pin names not known; wires that end beside it: relaydt_120_p1, relaydt_120_p2, relaydt_102_p6, relaydt_108_p10, relaydt_108_p8, relaydt_120_p1, relaydt_120_p1, relaydt_120_p2, 1'b0, relaydt_108_p4, relaydt_120_p11[0], 1'b1, relaydt_108_p5, REG_COUNT[1], 1'b0
  // RelayDT #(.poles(4)) relaydt_121: pin names not known; wires that end beside it: 1'b1, 1'b0, relaydt_121_p3, 1'b0, 1'b1, relaydt_121_p6, 1'b0, 1'b1, relaydt_121_p9, REG_C[3], 1'b0, 1'b0, 1'b1, relaydt_121_p14
  // RelayDT #(.poles(4)) relaydt_122: pin names not known; wires that end beside it: 1'b1, 1'b0, relaydt_122_p3[0], relaydt_121_p6, relaydt_121_p3, relaydt_122_p6[0], relaydt_121_p9, 1'b1, relaydt_122_p9[0], REG_B[3], 1'b0, 1'b0, relaydt_121_p14, relaydt_122_p14[0]
  LED led_79 (.in(relaydt_122_p9[0]));
  // RelayDT relaydt_123: pin names not known; wires that end beside it: relaydt_123_p1[0], 1'b1, 1'b0
  LED led_80 (.in(relaydt_130_p1[0]));
  // RelayDT #(.poles(2)) relaydt_124: pin names not known; wires that end beside it: relay_54_p4, relay_54_p4, REG_COUNT[1], 1'b0, relaydt_94_p7, 1'b1, 1'b0
  LED led_81 (.in(REG_COUNT[1]));
  // RelayDT relaydt_125: pin names not known; wires that end beside it: relaydt_108_p4, 1'b1, 1'b0
  // RelayDT relaydt_126: pin names not known; wires that end beside it: relaydt_108_p5, 1'b0, 1'b1, relaydt_126_p4, relaydt_126_p4, relaydt_126_p6
  LED led_82 (.in(relaydt_120_p11[0]));
  LED led_83 (.in(relaydt_122_p14[0]));
  // RelayDT #(.poles(4)) relaydt_127: pin names not known; wires that end beside it: relaydt_127_p1, relaydt_127_p2, relaydt_110_p6, relaydt_116_p10, relaydt_116_p8, relaydt_127_p1, relaydt_127_p1, relaydt_127_p2, 1'b0, relaydt_116_p4, relaydt_127_p11[0], 1'b1, relaydt_116_p5, REG_B[4], 1'b0
  // RelayDT #(.poles(4)) relaydt_128: pin names not known; wires that end beside it: relaydt_128_p1, relaydt_128_p2, relaydt_112_p6, relaydt_117_p10, relaydt_117_p8, relaydt_128_p1, relaydt_128_p1, relaydt_128_p2, 1'b0, relaydt_117_p4, relaydt_128_p11[0], 1'b1, relaydt_117_p5, REG_B[4], 1'b0
  // RelayDT relaydt_129: pin names not known; wires that end beside it: REG_B[4], 1'b0, relaydt_118_p6, REG_B[4], 1'b0, relaydt_129_p6, 1'b0
  // RelayDT relaydt_130: pin names not known; wires that end beside it: relaydt_130_p1[0], 1'b1, 1'b0
  // RelayDT #(.poles(4)) relaydt_131: pin names not known; wires that end beside it: relaydt_131_p1, _1_2[0], relaydt_131_p1, 1'b0, relaydt_131_p5, relaydt_131_p6, relaydt_126_p6, relaydt_131_p8, relaydt_131_p8, relaydt_131_p5, relaydt_131_p6
  LED led_84 (.in(relaydt_138_p6[0]));
  LED led_85 (.in(relaydt_138_p3[0]));
  // RelayDT relaydt_132: pin names not known; wires that end beside it: relaydt_116_p4, 1'b1, 1'b0
  // RelayDT relaydt_133: pin names not known; wires that end beside it: relaydt_116_p5, 1'b0, 1'b1, relaydt_133_p4, relaydt_133_p4, relaydt_133_p6
  LED led_86 (.in(relaydt_127_p11[0]));
  // RelayDT relaydt_134: pin names not known; wires that end beside it: relaydt_117_p4, 1'b1, 1'b0
  // RelayDT relaydt_135: pin names not known; wires that end beside it: relaydt_117_p5, 1'b0, 1'b1, relaydt_135_p4, relaydt_135_p4, relaydt_135_p6
  LED led_87 (.in(relaydt_128_p11[0]));
  // RelayDT relaydt_136: pin names not known; wires that end beside it: REG_B[3], 1'b0, relaydt_129_p6, REG_B[3], 1'b0, relaydt_136_p6, 1'b0
  LED led_88 (.in(relaydt_142_p1[0]));
  // Relay relay_55: pin names not known; wires that end beside it: relaydt_94_p4, relaydt_78_p5[0], 1'b0, relay_55_p4
  // RelayDT #(.poles(4)) relaydt_137: pin names not known; wires that end beside it: 1'b1, 1'b0, relaydt_137_p3, 1'b0, 1'b1, relaydt_137_p6, 1'b0, 1'b1, relaydt_137_p9, REG_C[2], 1'b0, 1'b0, 1'b1, relaydt_137_p14
  // RelayDT #(.poles(4)) relaydt_138: pin names not known; wires that end beside it: 1'b1, 1'b0, relaydt_138_p3[0], relaydt_137_p6, relaydt_137_p3, relaydt_138_p6[0], relaydt_137_p9, 1'b1, relaydt_138_p9[0], REG_B[2], 1'b0, 1'b0, relaydt_137_p14, relaydt_138_p14[0]
  LED led_89 (.in(relaydt_138_p9[0]));
  // RelayDT #(.poles(4)) relaydt_139: pin names not known; wires that end beside it: relaydt_139_p1, REG_C[3], relaydt_139_p1, relaydt_139_p4, relaydt_139_p5, 1'b0, relaydt_139_p7, relaydt_139_p8, relaydt_133_p6, relaydt_139_p10, relaydt_139_p10, relaydt_139_p7, relaydt_139_p8
  // RelayDT #(.poles(4)) relaydt_140: pin names not known; wires that end beside it: relaydt_140_p1, _1[3], relaydt_140_p1, relaydt_140_p4, relaydt_140_p5, 1'b0, relaydt_140_p7, relaydt_140_p8, relaydt_135_p6, relaydt_140_p10, relaydt_140_p10, relaydt_140_p7, relaydt_140_p8
  // RelayDT relaydt_141: pin names not known; wires that end beside it: REG_B[2], 1'b0, relaydt_136_p6, REG_B[2], 1'b0, relaydt_141_p6, 1'b0
  // RelayDT relaydt_142: pin names not known; wires that end beside it: relaydt_142_p1[0], 1'b1, 1'b0
  LED led_90 (.in(relaydt_146_p1[0]));
  // RelayDT #(.poles(2)) relaydt_143: pin names not known; wires that end beside it: relay_55_p4, relay_55_p4, REG_COUNT[0], 1'b0, relaydt_94_p7, 1'b1, 1'b0, in_41, 1'b0
  LED led_91 (.in(REG_COUNT[0]));
  // RelayDT #(.poles(4)) relaydt_144: pin names not known; wires that end beside it: relaydt_144_p1, relaydt_144_p2, relaydt_126_p6, relaydt_131_p8, relaydt_131_p6, relaydt_144_p1, relaydt_144_p1, relaydt_144_p2, 1'b0, 1'b1, relaydt_144_p11[0], 1'b1, 1'b0, REG_COUNT[0], relaydt_144_p15, 1'b0
  LED led_92 (.in(relaydt_144_p11[0]));
  LED led_93 (.in(relaydt_138_p14[0]));
  // RelayDT relaydt_145: pin names not known; wires that end beside it: REG_B[1], 1'b0, relaydt_141_p6, REG_B[1], 1'b0, relaydt_145_p6, 1'b0
  // RelayDT relaydt_146: pin names not known; wires that end beside it: relaydt_146_p1[0], 1'b1, 1'b0
  LED led_94 (.in(relaydt_149_p1[0]));
  LED led_95 (.in(relaydt_152_p6[0]));
  LED led_96 (.in(relaydt_152_p3[0]));
  // RelayDT #(.poles(4)) relaydt_147: pin names not known; wires that end beside it: relaydt_147_p1, relaydt_147_p2, relaydt_133_p6, relaydt_139_p10, relaydt_139_p8, relaydt_147_p1, relaydt_147_p1, relaydt_147_p2, 1'b0, relaydt_139_p4, relaydt_147_p11[0], 1'b1, relaydt_139_p5, REG_B[3], 1'b0
  LED led_97 (.in(relaydt_147_p11[0]));
  // RelayDT #(.poles(4)) relaydt_148: pin names not known; wires that end beside it: relaydt_148_p1, relaydt_148_p2, relaydt_135_p6, relaydt_140_p10, relaydt_140_p8, relaydt_148_p1, relaydt_148_p1, relaydt_148_p2, 1'b0, relaydt_140_p4, relaydt_148_p11[0], 1'b1, relaydt_140_p5, REG_B[3], 1'b0
  LED led_98 (.in(relaydt_148_p11[0]));
  // RelayDT relaydt_149: pin names not known; wires that end beside it: relaydt_149_p1[0], 1'b1, 1'b0
  LED led_99 (.in(relaydt_100_p1[0]));
  // Relay #(.Bits(8)) relay_56: pin names not known; wires that end beside it: {4'b0000, REG_COUNT}, 1'b0, BUS
  // RelayDT #(.poles(2)) relaydt_150: pin names not known; wires that end beside it: nCLOCK, 1'b1, relaydt_150_p3, relaydt_150_p4, relaydt_150_p3, 1'b0
  // Relay relay_57: pin names not known; wires that end beside it: relaydt_83_p11[1], relay_57_p2
  LED led_100 (.in(CIncrement[3]));
  // RelayDT #(.poles(4)) relaydt_151: pin names not known; wires that end beside it: 1'b1, 1'b0, relaydt_151_p3, 1'b0, 1'b1, relaydt_151_p6, 1'b0, 1'b1, relaydt_151_p9, REG_C[1], 1'b0, 1'b0, 1'b1, relaydt_151_p14
  // RelayDT #(.poles(4)) relaydt_152: pin names not known; wires that end beside it: 1'b1, 1'b0, relaydt_152_p3[0], relaydt_151_p6, relaydt_151_p3, relaydt_152_p6[0], relaydt_151_p9, 1'b1, relaydt_152_p9[0], REG_B[1], 1'b0, 1'b0, relaydt_151_p14, relaydt_152_p14[0]
  LED led_101 (.in(relaydt_152_p9[0]));
  // RelayDT relaydt_153: pin names not known; wires that end beside it: relaydt_139_p4, 1'b1, 1'b0
  // RelayDT relaydt_154: pin names not known; wires that end beside it: relaydt_139_p5, 1'b0, 1'b1, relaydt_154_p4, relaydt_154_p4, relaydt_154_p6
  // RelayDT relaydt_155: pin names not known; wires that end beside it: relaydt_140_p4, 1'b1, 1'b0
  // RelayDT relaydt_156: pin names not known; wires that end beside it: relaydt_140_p5, 1'b0, 1'b1, relaydt_156_p4, relaydt_156_p4, relaydt_156_p6
  // RelayDT relaydt_157: pin names not known; wires that end beside it: REG_B[0], 1'b0, relaydt_145_p6, REG_B[0], 1'b0, ZERO, 1'b0
  // RelayDT relaydt_158: pin names not known; wires that end beside it: 1'b1, relay_57_p2, relaydt_144_p15, 1'b0
  // RelayDT #(.poles(2)) relaydt_159: pin names not known; wires that end beside it: relay_57_p2, CIncrement[3], relaydt_150_p4, 1'b1, 1'b0
  LED led_102 (.in(relaydt_152_p14[0]));
  // RelayDT #(.poles(4)) relaydt_160: pin names not known; wires that end beside it: relaydt_160_p1, REG_C[2], relaydt_160_p1, relaydt_160_p4, relaydt_160_p5, 1'b0, relaydt_160_p7, relaydt_160_p8, relaydt_154_p6, relaydt_160_p10, relaydt_160_p10, relaydt_160_p7, relaydt_160_p8
  // RelayDT #(.poles(4)) relaydt_161: pin names not known; wires that end beside it: relaydt_161_p1, _1[2], relaydt_161_p1, relaydt_161_p4, relaydt_161_p5, 1'b0, relaydt_161_p7, relaydt_161_p8, relaydt_156_p6, relaydt_161_p10, relaydt_161_p10, relaydt_161_p7, relaydt_161_p8
  // Relay #(.Bits(8)) relay_58: pin names not known; wires that end beside it: in_30, {relaydt_114_p1, relaydt_123_p1[0], relaydt_130_p1[0], relaydt_142_p1[0], relaydt_146_p1[0], relaydt_149_p1[0], relaydt_100_p1[0]}, 1'b0, BUS
  // Relay relay_59: pin names not known; wires that end beside it: relaydt_144_p15, relaydt_83_p11[0], 1'b0, relay_59_p4
  LED led_103 (.in(relaydt_164_p6[0]));
  LED led_104 (.in(relaydt_164_p3[0]));
  // Relay #(.Bits(8)) relay_60: pin names not known; wires that end beside it: in_22, {relaydt_59_p3, relaydt_72_p14[0], relaydt_86_p14[0], relaydt_104_p14[0], relaydt_122_p14[0], relaydt_138_p14[0], relaydt_152_p14[0]}, BUS
  // RelayDT #(.poles(2)) relaydt_162: pin names not known; wires that end beside it: relay_59_p4, relay_59_p4, CIncrement[2], 1'b0, relaydt_150_p4, 1'b1, 1'b0
  LED led_105 (.in(CIncrement[2]));
  // RelayDT #(.poles(4)) relaydt_163: pin names not known; wires that end beside it: 1'b1, 1'b0, relaydt_163_p3, 1'b0, 1'b1, relaydt_163_p6, 1'b0, 1'b1, relaydt_163_p9, REG_C[0], 1'b0
  // RelayDT #(.poles(4)) relaydt_164: pin names not known; wires that end beside it: 1'b1, 1'b0, relaydt_164_p3[0], relaydt_163_p6, relaydt_163_p3, relaydt_164_p6[0], relaydt_163_p9, 1'b0, 1'b1, relaydt_164_p10[0], REG_B[0], 1'b0, in_23, 1'b0
  LED led_106 (.in(relaydt_164_p10[0]));
  // RelayDT relaydt_165: pin names not known; wires that end beside it: relaydt_160_p4, 1'b1, 1'b0
  // RelayDT relaydt_166: pin names not known; wires that end beside it: relaydt_160_p5, 1'b0, 1'b1, relaydt_166_p4, relaydt_166_p4, relaydt_166_p6
  // RelayDT #(.poles(4)) relaydt_167: pin names not known; wires that end beside it: relaydt_167_p1, relaydt_167_p2, relaydt_154_p6, relaydt_160_p10, relaydt_160_p8, relaydt_167_p1, relaydt_167_p1, relaydt_167_p2, 1'b0, relaydt_160_p4, relaydt_167_p11[0], 1'b1, relaydt_160_p5, REG_B[2], 1'b0
  LED led_107 (.in(relaydt_167_p11[0]));
  // RelayDT relaydt_168: pin names not known; wires that end beside it: relaydt_161_p4, 1'b1, 1'b0
  // RelayDT relaydt_169: pin names not known; wires that end beside it: relaydt_161_p5, 1'b0, 1'b1, relaydt_169_p4, relaydt_169_p4, relaydt_169_p6
  // RelayDT #(.poles(4)) relaydt_170: pin names not known; wires that end beside it: relaydt_170_p1, relaydt_170_p2, relaydt_156_p6, relaydt_161_p10, relaydt_161_p8, relaydt_170_p1, relaydt_170_p1, relaydt_170_p2, 1'b0, relaydt_161_p4, relaydt_170_p11[0], 1'b1, relaydt_161_p5, REG_B[2], 1'b0
  LED led_108 (.in(relaydt_170_p11[0]));
  // Relay #(.Bits(8)) relay_61: pin names not known; wires that end beside it: {relaydt_59_p12, relaydt_86_p9[0], relaydt_104_p9[0], relaydt_122_p9[0], relaydt_138_p9[0], relaydt_152_p9[0], relaydt_164_p10[0]}, in_24, BUS, 1'b0
  // Relay #(.Bits(8)) relay_62: pin names not known; wires that end beside it: {relaydt_59_p9, relaydt_86_p6[0], relaydt_104_p6[0], relaydt_122_p6[0], relaydt_138_p6[0], relaydt_152_p6[0], relaydt_164_p6[0]}, in_25, BUS, 1'b0
  // Relay #(.Bits(8)) relay_63: pin names not known; wires that end beside it: {relaydt_59_p6, relaydt_86_p3[0], relaydt_104_p3[0], relaydt_122_p3[0], relaydt_138_p3[0], relaydt_152_p3[0], relaydt_164_p3[0]}, BUS
  // RelayDT #(.poles(4)) relaydt_171: pin names not known; wires that end beside it: relaydt_171_p1, REG_C[1], relaydt_171_p1, relaydt_171_p4, relaydt_171_p5, 1'b0, relaydt_171_p7, relaydt_171_p8, relaydt_166_p6, relaydt_171_p10, relaydt_171_p10, relaydt_171_p7, relaydt_171_p8
  // RelayDT #(.poles(4)) relaydt_172: pin names not known; wires that end beside it: relaydt_172_p1, _1[1], relaydt_172_p1, relaydt_172_p4, relaydt_172_p5, 1'b0, relaydt_172_p7, relaydt_172_p8, relaydt_169_p6, relaydt_172_p10, relaydt_172_p10, relaydt_172_p7, relaydt_172_p8
  // RelayDT #(.poles(4)) relaydt_173: pin names not known; wires that end beside it: in_31[2], 1'b1, 1'b0, 1'b1, 1'b0, 1'b0, 1'b1, 1'b0, 1'b1, 1'b0, relaydt_173_p11, relaydt_173_p12, relaydt_173_p13, relaydt_173_p14, in_31[1], relaydt_173_p11, 1'b0, 1'b0, relaydt_173_p12, relaydt_173_p13, 1'b0, 1'b0, relaydt_173_p14
  // Relay relay_64: pin names not known; wires that end beside it: relaydt_144_p15, relaydt_120_p11[0], 1'b0, relay_64_p4
  LED led_109 (.in(CIncrement[1]));
  // RelayDT #(.poles(4)) relaydt_174: pin names not known; wires that end beside it: 1'b0, in_31[0]
  // RelayDT #(.poles(2)) relaydt_175: pin names not known; wires that end beside it: relay_64_p4, relay_64_p4, CIncrement[1], 1'b0, relaydt_150_p4, 1'b1, 1'b0
  // RelayDT #(.poles(4)) relaydt_176: pin names not known; wires that end beside it: relaydt_176_p1, relaydt_176_p2, relaydt_166_p6, relaydt_171_p10, relaydt_171_p8, relaydt_176_p1, relaydt_176_p1, relaydt_176_p2, 1'b0, relaydt_171_p4, relaydt_176_p11[0], 1'b1, relaydt_171_p5, REG_B[1], 1'b0
  // RelayDT #(.poles(4)) relaydt_177: pin names not known; wires that end beside it: relaydt_177_p1, relaydt_177_p2, relaydt_169_p6, relaydt_172_p10, relaydt_172_p8, relaydt_177_p1, relaydt_177_p1, relaydt_177_p2, 1'b0, relaydt_172_p4, relaydt_177_p11[0], 1'b1, relaydt_172_p5, REG_B[1], 1'b0
  // RelayDT #(.poles(8)) relaydt_178: pin names not known; wires that end beside it: relaydt_178_p1, 1'b0, 1'b0, relaydt_178_p1, relaydt_178_p5, 1'b0, 1'b0, relaydt_178_p5, relaydt_178_p9, 1'b0, 1'b0, relaydt_178_p9, relaydt_178_p13, 1'b0, 1'b0, relaydt_178_p13, 1'b0, in_30, in_25, in_24, in_23, in_22, in_29, in_26, relaydt_178_p25
  // Relay relay_65: pin names not known; wires that end beside it: relaydt_144_p15, relaydt_144_p11[0], 1'b0, relay_65_p4
  // RelayDT relaydt_179: pin names not known; wires that end beside it: relaydt_171_p4, 1'b1, 1'b0
  // RelayDT relaydt_180: pin names not known; wires that end beside it: relaydt_171_p5, 1'b0, 1'b1, relaydt_180_p4, relaydt_180_p4, relaydt_180_p6
  LED led_110 (.in(relaydt_176_p11[0]));
  // RelayDT relaydt_181: pin names not known; wires that end beside it: relaydt_172_p4, 1'b1, 1'b0
  // RelayDT relaydt_182: pin names not known; wires that end beside it: relaydt_172_p5, 1'b0, 1'b1, relaydt_182_p4, relaydt_182_p4, relaydt_182_p6
  LED led_111 (.in(relaydt_177_p11[0]));
  LED led_112 (.in(in_30));
  LED led_113 (.in(in_25));
  LED led_114 (.in(in_24));
  LED led_115 (.in(in_23));
  LED led_116 (.in(in_22));
  LED led_117 (.in(in_29));
  LED led_118 (.in(in_26));
  LED led_119 (.in(relaydt_178_p25));
  // RelayDT #(.poles(2)) relaydt_183: pin names not known; wires that end beside it: relay_65_p4, relay_65_p4, CIncrement[0], 1'b0, relaydt_150_p4, 1'b1, 1'b0
  LED led_120 (.in(CIncrement[0]));
  // RelayDT #(.poles(4)) relaydt_184: pin names not known; wires that end beside it: relaydt_184_p1, REG_C[0], relaydt_184_p1, 1'b0, relaydt_184_p5, relaydt_184_p6, relaydt_180_p6, relaydt_184_p8, relaydt_184_p8, relaydt_184_p5, relaydt_184_p6
  // RelayDT #(.poles(4)) relaydt_185: pin names not known; wires that end beside it: relaydt_185_p1, _1[0], relaydt_185_p1, 1'b0, relaydt_185_p5, relaydt_185_p6, relaydt_182_p6, relaydt_185_p8, relaydt_185_p8, relaydt_185_p5, relaydt_185_p6
  // RelayDT #(.poles(4)) relaydt_186: pin names not known; wires that end beside it: relaydt_186_p1, relaydt_186_p2, relaydt_180_p6, relaydt_184_p8, relaydt_184_p6, relaydt_186_p1, relaydt_186_p1, relaydt_186_p2, 1'b0, 1'b1, relaydt_186_p11[0], 1'b1, 1'b0, REG_B[0], in_26, 1'b0
  // RelayDT #(.poles(4)) relaydt_187: pin names not known; wires that end beside it: relaydt_187_p1, relaydt_187_p2, relaydt_182_p6, relaydt_185_p8, relaydt_185_p6, relaydt_187_p1, relaydt_187_p1, relaydt_187_p2, 1'b0, 1'b1, relaydt_187_p11[0], 1'b1, 1'b0, REG_B[0], in_29, 1'b0
  // Relay #(.Bits(8)) relay_66: pin names not known; wires that end beside it: {relaydt_68_p11, relaydt_105_p11[0], relaydt_127_p11[0], relaydt_147_p11[0], relaydt_167_p11[0], relaydt_176_p11[0], relaydt_186_p11[0]}, BUS
  LED led_121 (.in(relaydt_186_p11[0]));
  // Relay #(.Bits(8)) relay_67: pin names not known; wires that end beside it: {relaydt_69_p11, relaydt_106_p11[0], relaydt_128_p11[0], relaydt_148_p11[0], relaydt_170_p11[0], relaydt_177_p11[0], relaydt_187_p11[0]}, BUS
  LED led_122 (.in(relaydt_187_p11[0]));

  // Other names for the same wires on the sheet: REG_B[7] = B_SIGN; AND_E = in_22; CE = in_39; CO = in_41;
  //   INCB_E = in_29; J = in_40; LRAM = in_37; NOTB_E = in_25; OR_E = in_23; RESET = in_42; RLB = in_20; RLC = in_19;
  //   RLI = in_34; RML = in_35; ROL = in_32; RSB = in_21; RSC = in_18; RSI = in_33; SCZL = in_28; SHLB_E = in_30;
  //   SRAM = in_36; SUM_E = in_26; XOR_E = in_24

  // Notes on the sheet:
  //   clk: Hz: 4
  //   clk_2: Hz: 8
  //   clk_3: Hz: 16
  //   clk_4: Hz: 2
  //   MANUAL: default 1
  //   _1: default 1
  //   _1_2: default 1
  //   B Register
  //   C Register
  //   Inst Register
  //   Output Register
  //   Mem Address Register
  //   CLOCK
  //   ALU-Logic
  //   AND
  //   ALU-Arithmetic
  //   SCZ Register
  //   Counter
  //   XOR
  //   NOT_B
  //   OR
  //   SUM
  //   SHL
  //   3-8 Decoder - no Z
endmodule
