// Digital circuit risc_like_8bit_digital.dig as structural Verilog
module risc_like_8bit_digital (
  input  clk,
  input  HALT,
  input  in_3,
  input  clk_2,
  input  clk_3,
  input  in_6,
  input  clk_4,
  input  MANUAL,
  input  [7:0] in_9,
  input  Manual_Load_BUS,
  input  in_11,
  input  in_12,
  input  in_13
);

  wire add_1_c_o, and_1_out, and_2_out, CLK_A, CLK_B, CLOCK, comparator_1_eq, comparator_2_eq,
       comparator_3_eq, comparator_4_eq, decoder_1_out_0, decoder_1_out_1, decoder_2_out_1, decoder_2_out_3,
       delay_1_out, nCLOCK, or_1_out, or_3_out, or_4_out, or_5_out, relaydt_1_p7, relaydt_1_p8, relaydt_2_p2,
       rs_ff_1_nq, rs_ff_1_q, STEP_out;
  wire [1:0] counter_1_out;
  wire [3:0] binary_to_bcd_1__1s, binary_to_bcd_1__10s, binary_to_bcd_1__100s;
  wire [5:0] DEST, SOURCE;
  wire [7:0] add_1_s, add_3_s, ADD_IN1_val, ADD_IN2_val, bitextender_1_out, BUS, multiplexer_1_out,
       multiplexer_2_out, multiplexer_3_out, multiplexer_4_out, Output_Register_q, PC, PC_INC_q, REG_A_val;
  wire [15:6] eepromdualport_1_d;

  // RelayDT #(.poles(2)) relaydt_1: pin names not known; wires that end beside it: in_6, clk_3, clk_2, clk, clk_4, 1'b0, relaydt_1_p7, relaydt_1_p8, in_3, relaydt_1_p7, relaydt_1_p8
  or or_1 (or_1_out, HALT, in_12);
  EEPROMDualPort #(.AddrBits(8), .Bits(16)) eepromdualport_1 (
    .A(PC), .Din({16{1'b0}}), .str(1'b0), .C(CLOCK), .ld(1'b1), .D({eepromdualport_1_d, DEST}));
  // RelayDT relaydt_2: pin names not known; wires that end beside it: 1'b0, relaydt_2_p2
  Button STEP (.out(STEP_out));
  and and_1 (and_1_out, STEP_out, MANUAL, ~or_1_out);  // And
  RS_FF rs_ff_1 (.S(and_2_out), .C(relaydt_2_p2), .R(~and_2_out), .Q(rs_ff_1_q), .nQ(rs_ff_1_nq));
  Decoder #(.Selector_Bits(2)) decoder_1 (
    .sel(eepromdualport_1_d[15:14]), .out_0(decoder_1_out_0), .out_1(decoder_1_out_1));  // open: out_2, out_3
  and and_2 (and_2_out, ~MANUAL, ~or_1_out, rs_ff_1_nq);  // And
  or or_2 (CLOCK, and_1_out, rs_ff_1_q);
  assign SOURCE = decoder_1_out_0 ? eepromdualport_1_d[11:6] : 6'bz;  // Driver driver_1
  assign BUS = decoder_1_out_1 ? eepromdualport_1_d[13:6] : 8'bz;  // Driver driver_2
  not not_1 (nCLOCK, CLOCK);
  Counter #(.Bits(2)) counter_1 (.en(1'b1), .C(CLOCK), .clr(and_2_out), .out(counter_1_out));  // open: ovf
  LED led_1 (.in(CLOCK));
  LED led_2 (.in(nCLOCK));
  LED led_3 (.in(BUS[7]));
  Decoder #(.Selector_Bits(2)) decoder_2 (
    .sel(counter_1_out), .out_1(decoder_2_out_1), .out_3(decoder_2_out_3));  // open: out_0, out_2
  LED led_4 (.in(decoder_2_out_1));
  LED led_5 (.in(decoder_2_out_3));
  LED led_6 (.in(BUS[5]));
  LED led_7 (.in(BUS[6]));
  LED led_8 (.in(BUS[3]));
  LED led_9 (.in(BUS[4]));
  assign BUS = Manual_Load_BUS ? in_9 : 8'bz;  // Driver driver_3
  LED led_10 (.in(BUS[1]));
  LED led_11 (.in(BUS[2]));
  LED led_12 (.in(BUS[0]));
  Button STEPA (.out(CLK_A));
  Button STEPB (.out(CLK_B));
  Register #(.Bits(8)) Output_Register (.D(BUS), .C(CLOCK), .en(in_13), .Q(Output_Register_q));
  Binary_to_BCD binary_to_bcd_1 (
    .In(Output_Register_q), ._100s(binary_to_bcd_1__100s), ._10s(binary_to_bcd_1__10s),
    ._1s(binary_to_bcd_1__1s));
  controlled_register REG_A (
    .IN(BUS), .SRC(SOURCE), .REG(6'b000011), .DST(DEST), .CLK(CLK_A), .RST(in_11), .VAL(REG_A_val), .OUT(BUS));
  controlled_register ADD_IN1 (
    .IN(BUS), .SRC(SOURCE), .REG(6'b001111), .DST(DEST), .CLK(CLK_A), .RST(in_11), .VAL(ADD_IN1_val));  // open: OUT
  controlled_register ADD_IN2 (
    .IN(BUS), .SRC(SOURCE), .REG(6'b010000), .DST(DEST), .CLK(CLK_A), .RST(in_11), .VAL(ADD_IN2_val));  // open: OUT
  controlled_register ADD_CARRY (
    .IN(bitextender_1_out), .SRC(SOURCE), .REG(6'b010001), .DST(DEST), .CLK(CLK_A), .RST(in_11));  // open: VAL, OUT
  Seven_Seg_Hex seven_seg_hex_1 (.d(binary_to_bcd_1__100s), .dp(1'b0));
  LED led_13 (.in(REG_A_val[7]));
  Seven_Seg_Hex seven_seg_hex_2 (.d(binary_to_bcd_1__10s), .dp(1'b0));
  Seven_Seg_Hex seven_seg_hex_3 (.d(binary_to_bcd_1__1s), .dp(1'b0));
  LED led_14 (.in(REG_A_val[6]));
  LED led_15 (.in(REG_A_val[5]));
  LED led_16 (.in(REG_A_val[4]));
  LED led_17 (.in(REG_A_val[3]));
  Add #(.Bits(8)) add_1 (.a(ADD_IN1_val), .b(ADD_IN2_val), .c_i(1'b0), .s(add_1_s), .c_o(add_1_c_o));
  Comparator #(.Bits(6)) comparator_1 (.a(SOURCE), .b(6'b000010), .eq(comparator_1_eq));  // open: gt, lt
  Comparator #(.Bits(6)) comparator_2 (.a(DEST), .b(6'b000010), .eq(comparator_2_eq));  // open: gt, lt
  LED led_18 (.in(REG_A_val[2]));
  LED led_19 (.in(REG_A_val[1]));
  LED led_20 (.in(REG_A_val[0]));
  BitExtender #(.inputBits(1), .outputBits(8)) bitextender_1 (.in(add_1_c_o), .out(bitextender_1_out));
  Multiplexer #(.Bits(8)) multiplexer_1 (.sel(in_11), .in_0(BUS), .in_1({8{1'b0}}), .out(multiplexer_1_out));
  or or_3 (or_3_out, in_11, CLK_B, comparator_2_eq);
  or or_4 (or_4_out, CLK_B, CLK_A);
  controlled_output ADD_2 (.SRC(SOURCE), .REG(6'b010000), .VAL(add_1_s), .OUT(BUS));
  Multiplexer #(.Bits(8)) multiplexer_2 (
    .sel(CLK_B), .in_0(multiplexer_1_out), .in_1(PC_INC_q), .out(multiplexer_2_out));
  Register #(.Bits(8)) Program_Counter (.D(multiplexer_2_out), .C(or_4_out), .en(or_3_out), .Q(PC));
  LED led_21 (.in(PC[7]));
  assign BUS = comparator_1_eq ? PC : 8'bz;  // Driver driver_4
  LED led_22 (.in(PC[6]));
  LED led_23 (.in(PC[5]));
  LED led_24 (.in(PC[4]));
  LED led_25 (.in(PC[3]));
  LED led_26 (.in(PC[2]));
  LED led_27 (.in(PC[1]));
  LED led_28 (.in(PC[0]));
  Add #(.Bits(8)) add_3 (.a(PC), .b({8{1'b0}}), .c_i(1'b1), .s(add_3_s));  // open: c_o
  Comparator #(.Bits(6)) comparator_3 (.a(SOURCE), .b(6'b100001), .eq(comparator_3_eq));  // open: gt, lt
  Comparator #(.Bits(6)) comparator_4 (.a(DEST), .b(6'b100001), .eq(comparator_4_eq));  // open: gt, lt
  Multiplexer #(.Bits(8)) multiplexer_3 (.sel(comparator_4_eq), .in_0(add_3_s), .in_1(BUS), .out(multiplexer_3_out));
  Multiplexer #(.Bits(8)) multiplexer_4 (
    .sel(in_11), .in_0(multiplexer_3_out), .in_1({8{1'b0}}), .out(multiplexer_4_out));
  or or_5 (or_5_out, in_11, CLK_A, comparator_4_eq);
  Delay #(.delayTime(2)) delay_1 (.in(CLK_A), .out(delay_1_out));
  Register #(.Bits(8)) PC_INC (.D(multiplexer_4_out), .C(delay_1_out), .en(or_5_out), .Q(PC_INC_q));
  assign BUS = comparator_3_eq ? PC_INC_q : 8'bz;  // Driver driver_5

  // Other names for the same wires on the sheet: HALT_t = in_12; RESET = in_11

  // Notes on the sheet:
  //   clk: Hz: 8
  //   clk_2: Hz: 16
  //   clk_3: Hz: 64
  //   clk_4: Hz: 2
  //   MANUAL: default 1
  //   CLOCK
  //   contents of eepromdualport_1 (hex, n*v repeats v):
  //   404f,4190,403
endmodule
